# Fritzing sketch arduino waterer nano pcb (saved by Fritzing 0.9.2b)
circuit board: 5.92cm x 5.92cm
perfboards: 1

parts:
  Part3 = Arduino Nano (Rev3.0)
  J2 = Power Jack [package=power_jack_combo]
  R5 = Resistor [tolerance=±5% resistance=220 package=THT]
  R6 = Resistor [tolerance=±5% resistance=220 package=THT]
  R7 = Resistor [tolerance=±5% resistance=220 package=THT]
  Q3 = Basic FET P-Channel [package="TO220 [THT]"]
  R8 = Rotary Potentiometer (Large) [maximum_resistance=100kΩ package=THT]

nets:
  N1: Part3.GND, Q3.source
  N2: Part3.D2, Q3.gate
  N3: Part3.D3, R7.Pin_0
  N4: Part3.D5, R6.Pin_0
  N5: Part3.D6, R5.Pin_0
  N6: Part3.VIN, J2.PWR
  N7: Part3.5V, R8.leg1
  N8: Part3.A4, R8.wiper
  N9: J2.GND, R8.leg2
